// Logisim project SOBOL.circ as structural Verilog: 11 circuits, main circuit main
module main (
);

  wire clock_1_out, comparator_1_eq, comparator_1_gt, controlled_buffer_1_out, controlled_buffer_2_out,
       controlled_buffer_21_out, controlled_buffer_22_out, equals_1_res, equals_2_res, equals_3_res,
       equals_4_res, equals_5_res, equals_6_res, equals_7_res, equals_8_res, equals_9_res, equals_10_res,
       equals_11_res, equals_12_res, equals_13_res, equals_14_res, equals_15_res, equals_16_res,
       equals_17_res, equals_18_res, equals_19_res, equals_20_res, equals_21_res, equals_22_res,
       equals_23_res, equals_24_res, equals_25_res, equals_26_res, equals_27_res, equals_28_res,
       equals_29_res, equals_30_res, nctotf_1_res, nctotf_2_res, nctotf_3_res, nctotf_4_res, nctotf_5_res,
       nctotf_6_res, nctotf_7_res, nctotf_8_res, nctotf_9_res, nctotf_10_res, nctotf_11_res, nctotf_12_res,
       nctotf_13_res, nctotf_14_res, nctotf_15_res, nctotf_16_res, nctotf_17_res, nctotf_18_res,
       nctotf_19_res, nctotf_20_res, nctotf_21_res, nctotf_22_res, nctotf_23_res, nctotf_24_res,
       nctotf_25_res, nctotf_26_res, nctotf_27_res, nctotf_28_res, not_1_out, or_1_out, or_2_out, or_3_out,
       or_4_out, or_5_out, por_1_out, Prepare_Register_q, register_9_q, register_10_q, register_11_q,
       register_12_q, register_13_q, register_15_q, register_16_q, RESET_out, smallor_1_out_3,
       smallor_2_out_3, smallor_3_out_3, smallor_4_out_3, smallor_5_out_3, smallor_6_out_3, smallor_7_out_3,
       smallor_8_out_3, summod_1_carryout, summod_1_halfcarryout, undriven, undriven_2, undriven_3,
       undriven_4, undriven_5, undriven_6, undriven_7, undriven_8, undriven_9, undriven_10, undriven_11,
       undriven_12, undriven_13, undriven_14, undriven_15, undriven_16, undriven_17, undriven_18,
       undriven_19, undriven_20, undriven_21, undriven_22, undriven_23, undriven_24, undriven_25,
       undriven_26, undriven_27;
  wire [7:0] buscontrol_1_out_6, buscontrol_1_out_8, buscontrol_2_out_6, buscontrol_2_out_7,
       buscontrol_3_out_6, buscontrol_3_out_7, buscontrol_3_out_8, buscontrol_3_out_9,
       controlled_buffer_3_out, controlled_buffer_4_out, controlled_buffer_24_out, controlled_buffer_25_out,
       Main_Counter_q, Main_Programm_p2, Main_Programm_p3, Main_Programm_p4, Main_Programm_p5,
       multiplexer_1_out, multiplier_1_out, register_1_q, register_2_q, register_3_q, register_4_q,
       register_5_q, register_6_q, register_7_q, register_8_q, summod_1_result, Watchdog_Timer_Counter_q,
       Watchdog_Timer_sw8;

  Clock clock_1 (.out(clock_1_out));
  Counter Main_Counter (
    .clr(or_2_out), .load(nctotf_2_res), .up(undriven_3), .count(not_1_out), .clk(controlled_buffer_1_out),
    .D(buscontrol_2_out_7), .Q(Main_Counter_q));  // open: carry
  // NoConnect on undriven_3
  not not_1 (not_1_out, nctotf_2_res);
  Register #(.trigger("falling"), .width(1)) Prepare_Register (
    .D(1'b1), .en(1'b1), .clk(or_3_out), .Q(Prepare_Register_q), .clr(undriven));
  Counter #(.ongoal("stay")) Watchdog_Timer_Counter (
    .count(or_1_out), .clk(or_3_out), .Q(Watchdog_Timer_Counter_q));  // open: clr, load, up, D, carry
  or or_1 (or_1_out, undriven, undriven_2);
  or or_2 (or_2_out, RESET_out, nctotf_1_res, por_1_out);
  Button RESET (.out(RESET_out));
  NCtoTF nctotf_1 (.A(controlled_buffer_2_out), .res(nctotf_1_res));
  POR #(.PorHighDuration(1)) por_1 (.out(por_1_out));
  DipSwitch Watchdog_Timer (
    .sw1(Watchdog_Timer_sw8[7]), .sw2(Watchdog_Timer_sw8[6]), .sw3(Watchdog_Timer_sw8[5]),
    .sw4(Watchdog_Timer_sw8[4]), .sw5(Watchdog_Timer_sw8[3]), .sw6(Watchdog_Timer_sw8[2]),
    .sw7(Watchdog_Timer_sw8[1]), .sw8(Watchdog_Timer_sw8[0]));
  assign controlled_buffer_1_out = Prepare_Register_q ? or_3_out : 1'bz;  // Controlled_Buffer controlled_buffer_1
  or or_3 (or_3_out, por_1_out, clock_1_out);
  // Probe on Watchdog_Timer_Counter_q
  // Probe on Watchdog_Timer_sw8
  Multiplier multiplier_1 (.a(8'h4), .b(Main_Counter_q), .out(multiplier_1_out));  // open: cin, cout
  Comparator #(.mode("unsigned")) comparator_1 (
    .a(Watchdog_Timer_Counter_q), .b(Watchdog_Timer_sw8), .gt(comparator_1_gt), .eq(comparator_1_eq));  // open: lt
  // ROM #(.addrWidth(10), .line("quad")) Main_Programm: pin names not known; wires that end beside it: {2'b00, multiplier_1_out}, Main_Programm_p2, Main_Programm_p3, Main_Programm_p4, Main_Programm_p5
  // Probe on buscontrol_2_out_6
  // Probe on buscontrol_2_out_7
  assign controlled_buffer_2_out = register_16_q ? or_4_out : 1'bz;  // Controlled_Buffer controlled_buffer_2
  or or_4 (or_4_out, comparator_1_gt, comparator_1_eq);
  Equals equals_1 (.A(buscontrol_2_out_6), .B(8'h40), .res(equals_1_res));
  NCtoTF nctotf_2 (.A(equals_1_res), .res(nctotf_2_res));
  Register register_1 (.D(buscontrol_2_out_7), .en(nctotf_3_res), .clk(or_3_out), .Q(register_1_q), .clr(undriven));
  Equals equals_2 (.A(buscontrol_2_out_6), .B({8{1'b0}}), .res(equals_2_res));
  NCtoTF nctotf_3 (.A(equals_2_res), .res(nctotf_3_res));
  Register register_2 (.D(buscontrol_2_out_7), .en(nctotf_4_res), .clk(or_3_out), .Q(register_2_q), .clr(undriven));
  Equals equals_3 (.A(buscontrol_2_out_6), .B(8'h1), .res(equals_3_res));
  NCtoTF nctotf_4 (.A(equals_3_res), .res(nctotf_4_res));
  Register register_3 (.D(buscontrol_2_out_7), .en(nctotf_5_res), .clk(or_3_out), .Q(register_3_q), .clr(undriven));
  Equals equals_4 (.A(buscontrol_2_out_6), .B(8'h2), .res(equals_4_res));
  NCtoTF nctotf_5 (.A(equals_4_res), .res(nctotf_5_res));
  Register register_4 (.D(buscontrol_2_out_7), .en(nctotf_6_res), .clk(or_3_out), .Q(register_4_q), .clr(undriven));
  Equals equals_5 (.A(buscontrol_2_out_6), .B(8'h3), .res(equals_5_res));
  NCtoTF nctotf_6 (.A(equals_5_res), .res(nctotf_6_res));
  Register register_5 (.D(buscontrol_2_out_7), .en(nctotf_7_res), .clk(or_3_out), .Q(register_5_q), .clr(undriven));
  Equals equals_6 (.A(buscontrol_2_out_6), .B(8'h4), .res(equals_6_res));
  NCtoTF nctotf_7 (.A(equals_6_res), .res(nctotf_7_res));
  Register register_6 (.D(buscontrol_2_out_7), .en(nctotf_8_res), .clk(or_3_out), .Q(register_6_q));  // open: clr
  Equals equals_7 (.A(buscontrol_2_out_6), .B(8'h5), .res(equals_7_res));
  NCtoTF nctotf_8 (.A(equals_7_res), .res(nctotf_8_res));
  Register register_7 (.D(buscontrol_2_out_7), .en(nctotf_9_res), .clk(or_3_out), .Q(register_7_q));  // open: clr
  Equals equals_8 (.A(buscontrol_2_out_6), .B(8'h6), .res(equals_8_res));
  NCtoTF nctotf_9 (.A(equals_8_res), .res(nctotf_9_res));
  Register register_8 (.D(buscontrol_2_out_7), .en(nctotf_10_res), .clk(or_3_out), .Q(register_8_q));  // open: clr
  Equals equals_9 (.A(buscontrol_2_out_6), .B(8'h7), .res(equals_9_res));
  NCtoTF nctotf_10 (.A(equals_9_res), .res(nctotf_10_res));
  Equals equals_10 (.A(buscontrol_1_out_8), .B(8'h40), .res(equals_10_res));
  NCtoTF nctotf_11 (.A(equals_10_res), .res(nctotf_11_res));
  assign controlled_buffer_3_out = nctotf_11_res ? Main_Counter_q : 8'bz;  // Controlled_Buffer controlled_buffer_3
  Equals equals_11 (.A(buscontrol_1_out_6), .B(8'h40), .res(equals_11_res));
  NCtoTF nctotf_12 (.A(equals_11_res), .res(nctotf_12_res));
  assign controlled_buffer_4_out = nctotf_12_res ? Main_Counter_q : 8'bz;  // Controlled_Buffer controlled_buffer_4
  Equals equals_12 (.A(buscontrol_1_out_8), .B({8{1'b0}}), .res(equals_12_res));
  NCtoTF nctotf_13 (.A(equals_12_res), .res(nctotf_13_res));
  assign controlled_buffer_3_out = nctotf_13_res ? register_1_q : 8'bz;  // Controlled_Buffer controlled_buffer_5
  Equals equals_13 (.A(buscontrol_1_out_6), .B({8{1'b0}}), .res(equals_13_res));
  NCtoTF nctotf_14 (.A(equals_13_res), .res(nctotf_14_res));
  assign controlled_buffer_4_out = nctotf_14_res ? register_1_q : 8'bz;  // Controlled_Buffer controlled_buffer_6
  Equals equals_14 (.A(buscontrol_1_out_8), .B(8'h1), .res(equals_14_res));
  NCtoTF nctotf_15 (.A(equals_14_res), .res(nctotf_15_res));
  assign controlled_buffer_3_out = nctotf_15_res ? register_2_q : 8'bz;  // Controlled_Buffer controlled_buffer_7
  Equals equals_15 (.A(buscontrol_1_out_6), .B(8'h1), .res(equals_15_res));
  NCtoTF nctotf_16 (.A(equals_15_res), .res(nctotf_16_res));
  assign controlled_buffer_4_out = nctotf_16_res ? register_2_q : 8'bz;  // Controlled_Buffer controlled_buffer_8
  Equals equals_16 (.A(buscontrol_1_out_8), .B(8'h2), .res(equals_16_res));
  NCtoTF nctotf_17 (.A(equals_16_res), .res(nctotf_17_res));
  assign controlled_buffer_3_out = nctotf_17_res ? register_3_q : 8'bz;  // Controlled_Buffer controlled_buffer_9
  Equals equals_17 (.A(buscontrol_1_out_6), .B(8'h2), .res(equals_17_res));
  NCtoTF nctotf_18 (.A(equals_17_res), .res(nctotf_18_res));
  assign controlled_buffer_4_out = nctotf_18_res ? register_3_q : 8'bz;  // Controlled_Buffer controlled_buffer_10
  Equals equals_18 (.A(buscontrol_1_out_8), .B(8'h3), .res(equals_18_res));
  NCtoTF nctotf_19 (.A(equals_18_res), .res(nctotf_19_res));
  assign controlled_buffer_3_out = nctotf_19_res ? register_4_q : 8'bz;  // Controlled_Buffer controlled_buffer_11
  Equals equals_19 (.A(buscontrol_1_out_6), .B(8'h3), .res(equals_19_res));
  NCtoTF nctotf_20 (.A(equals_19_res), .res(nctotf_20_res));
  assign controlled_buffer_4_out = nctotf_20_res ? register_4_q : 8'bz;  // Controlled_Buffer controlled_buffer_12
  Equals equals_20 (.A(buscontrol_1_out_8), .B(8'h4), .res(equals_20_res));
  NCtoTF nctotf_21 (.A(equals_20_res), .res(nctotf_21_res));
  assign controlled_buffer_3_out = nctotf_21_res ? register_5_q : 8'bz;  // Controlled_Buffer controlled_buffer_13
  Equals equals_21 (.A(buscontrol_1_out_6), .B(8'h4), .res(equals_21_res));
  NCtoTF nctotf_22 (.A(equals_21_res), .res(nctotf_22_res));
  assign controlled_buffer_4_out = nctotf_22_res ? register_5_q : 8'bz;  // Controlled_Buffer controlled_buffer_14
  Equals equals_22 (.A(buscontrol_1_out_8), .B(8'h5), .res(equals_22_res));
  NCtoTF nctotf_23 (.A(equals_22_res), .res(nctotf_23_res));
  assign controlled_buffer_3_out = nctotf_23_res ? register_6_q : 8'bz;  // Controlled_Buffer controlled_buffer_15
  Equals equals_23 (.A(buscontrol_1_out_6), .B(8'h5), .res(equals_23_res));
  NCtoTF nctotf_24 (.A(equals_23_res), .res(nctotf_24_res));
  assign controlled_buffer_4_out = nctotf_24_res ? register_6_q : 8'bz;  // Controlled_Buffer controlled_buffer_16
  Equals equals_24 (.A(buscontrol_1_out_8), .B(8'h6), .res(equals_24_res));
  NCtoTF nctotf_25 (.A(equals_24_res), .res(nctotf_25_res));
  assign controlled_buffer_3_out = nctotf_25_res ? register_7_q : 8'bz;  // Controlled_Buffer controlled_buffer_17
  Equals equals_25 (.A(buscontrol_1_out_6), .B(8'h6), .res(equals_25_res));
  NCtoTF nctotf_26 (.A(equals_25_res), .res(nctotf_26_res));
  assign controlled_buffer_4_out = nctotf_26_res ? register_7_q : 8'bz;  // Controlled_Buffer controlled_buffer_18
  Equals equals_26 (.A(buscontrol_1_out_8), .B(8'h7), .res(equals_26_res));
  NCtoTF nctotf_27 (.A(equals_26_res), .res(nctotf_27_res));
  assign controlled_buffer_3_out = nctotf_27_res ? register_8_q : 8'bz;  // Controlled_Buffer controlled_buffer_19
  Equals equals_27 (.A(buscontrol_1_out_6), .B(8'h7), .res(equals_27_res));
  NCtoTF nctotf_28 (.A(equals_27_res), .res(nctotf_28_res));
  assign controlled_buffer_4_out = nctotf_28_res ? register_8_q : 8'bz;  // Controlled_Buffer controlled_buffer_20
  // Probe on Main_Programm_p2
  // Probe on Main_Programm_p3
  busControl buscontrol_1 (
    .in_1(buscontrol_3_out_8), .in_3(buscontrol_3_out_7), .in_5(Prepare_Register_q),
    .out_6(buscontrol_1_out_6), .out_8(buscontrol_1_out_8));  // open: in_2, in_4, out_7, out_9
  busControl buscontrol_2 (
    .in_1(controlled_buffer_25_out), .in_2(controlled_buffer_24_out), .in_5(Prepare_Register_q),
    .out_6(buscontrol_2_out_6), .out_7(buscontrol_2_out_7));  // open: in_3, in_4, out_8, out_9
  // Probe on Main_Programm_p4
  // Probe on Main_Programm_p5
  busControl buscontrol_3 (
    .in_1(Main_Programm_p2), .in_2(Main_Programm_p3), .in_3(Main_Programm_p4), .in_4(Main_Programm_p5),
    .in_5(Prepare_Register_q), .out_6(buscontrol_3_out_6), .out_7(buscontrol_3_out_7),
    .out_8(buscontrol_3_out_8), .out_9(buscontrol_3_out_9));
  Equals equals_28 (.A(buscontrol_3_out_6), .B(8'h1), .res(equals_28_res));
  Equals equals_29 (.A(buscontrol_3_out_6), .B(8'h2), .res(equals_29_res));
  Equals equals_30 (.A(buscontrol_3_out_6), .B(8'h3), .res(equals_30_res));
  Multiplexer #(.width(8)) multiplexer_1 (
    .in0(controlled_buffer_4_out), .in1(buscontrol_3_out_8), .out(multiplexer_1_out), .sel(equals_30_res));
  or or_5 (or_5_out, equals_28_res, equals_29_res, equals_30_res);
  SumMod summod_1 (
    .A(controlled_buffer_3_out), .B(multiplexer_1_out), .CarryIN(controlled_buffer_21_out),
    .CarryOUT(summod_1_carryout), .HalfCarryOUT(summod_1_halfcarryout), .Result(summod_1_result));
  assign controlled_buffer_21_out = equals_28_res ? register_9_q : 1'bz;  // Controlled_Buffer controlled_buffer_21
  assign controlled_buffer_22_out = or_5_out ? summod_1_halfcarryout : 1'bz;  // Controlled_Buffer controlled_buffer_22
  Register #(.width(1)) register_9 (
    .D(undriven_4), .en(undriven_5), .clk(or_3_out), .Q(register_9_q), .clr(smallor_1_out_3));
  assign register_9_q = or_5_out ? summod_1_carryout : 1'bz;  // Controlled_Buffer controlled_buffer_23
  Register #(.width(1)) register_10 (
    .D(undriven_7), .en(undriven_8), .clk(or_3_out), .Q(register_10_q), .clr(smallor_2_out_3));
  smallOR smallor_1 (.in_1(undriven_6), .in_2(undriven), .out_3(smallor_1_out_3));
  bigControledBuffer bigcontroledbuffer_1 (
    .A(or_5_out), .enable(or_5_out));  // open: B_0, B_1, B_2, B_3, B_4, B_5, B_6, B_7
  smallOR smallor_2 (.in_1(undriven_9), .in_2(undriven), .out_3(smallor_2_out_3));
  LedBar ledbar_1 (
    .led0(register_9_q), .led1(register_10_q), .led2(register_11_q), .led3(register_12_q),
    .led4(register_13_q), .led5(controlled_buffer_22_out), .led6(register_15_q), .led7(register_16_q));
  Register #(.width(1)) register_11 (
    .D(undriven_10), .en(undriven_11), .clk(or_3_out), .Q(register_11_q), .clr(smallor_3_out_3));
  smallOR smallor_3 (.in_1(undriven_12), .in_2(undriven), .out_3(smallor_3_out_3));
  Register #(.width(1)) register_12 (
    .D(undriven_13), .en(undriven_14), .clk(or_3_out), .Q(register_12_q), .clr(smallor_4_out_3));
  smallOR smallor_4 (.in_1(undriven_15), .in_2(undriven), .out_3(smallor_4_out_3));
  Register #(.width(1)) register_13 (
    .D(undriven_16), .en(undriven_17), .clk(or_3_out), .Q(register_13_q), .clr(smallor_5_out_3));
  Register #(.width(1)) register_14 (
    .D(undriven_19), .en(undriven_20), .clk(or_3_out), .Q(controlled_buffer_22_out), .clr(smallor_6_out_3));
  smallOR smallor_5 (.in_1(undriven_18), .in_2(undriven), .out_3(smallor_5_out_3));
  smallOR smallor_6 (.in_1(undriven_21), .in_2(undriven), .out_3(smallor_6_out_3));
  Register #(.width(1)) register_15 (
    .D(undriven_22), .en(undriven_23), .clk(or_3_out), .Q(register_15_q), .clr(smallor_7_out_3));
  smallOR smallor_7 (.in_1(undriven_24), .in_2(undriven), .out_3(smallor_7_out_3));
  Register #(.width(1)) register_16 (
    .D(undriven_25), .en(undriven_26), .clk(or_3_out), .Q(register_16_q), .clr(smallor_8_out_3));
  smallOR smallor_8 (.in_1(undriven_27), .in_2(undriven), .out_3(smallor_8_out_3));
  assign controlled_buffer_24_out = or_5_out ? summod_1_result : 8'bz;  // Controlled_Buffer controlled_buffer_24
  assign controlled_buffer_25_out = or_5_out ? buscontrol_3_out_9 : 8'bz;  // Controlled_Buffer controlled_buffer_25

  // Notes on the sheet:
  //   contents of Main_Programm (hex, n*v repeats v):
  //   3 1 f 1 3 2 1 2 1 1 2 3
  //   RED ADDR
  //   RES DATA
  //   MAIN DATA BUS
  //   OPCODE
  //   ADDR1
  //   SOBOL-0
  //   rev5
  //   ADDR2
  //   RESADDR
  //   RESET LINE
  //   MAIN PROGRAMM BUS
  //   C
  //   Z
  //   N
  //   SREG
  //   V
  //   S
  //   H
  //   T
  //   I
endmodule

// АЛП
module ALU (
  input  [7:0] opcode,
  input  [7:0] A,
  input  [7:0] B,
  output Carry,
  output [7:0] Result
);

  wire adder_1_cout, decoder_1_out0, decoder_1_out1, decoder_1_out2, decoder_1_out3, decoder_1_out4,
       decoder_1_out5, subtractor_1_bout;
  wire [7:0] adder_1_out, and_1_out, not_1_out, or_1_out, subtractor_1_out, xor_1_out;

  Decoder #(.enable("false"), .select(3)) decoder_1 (
    .out0(decoder_1_out0), .out1(decoder_1_out1), .out2(decoder_1_out2), .out3(decoder_1_out3),
    .out4(decoder_1_out4), .out5(decoder_1_out5), .sel(opcode[2:0]));  // open: out6, out7
  Adder adder_1 (.a(A), .b(B), .out(adder_1_out), .cout(adder_1_cout));  // open: cin
  Subtractor subtractor_1 (.a(A), .b(B), .out(subtractor_1_out), .bout(subtractor_1_bout));  // open: bin
  assign and_1_out = A & B;  // AND_Gate and_1, 8 bits wide
  assign or_1_out = A | B;  // OR_Gate or_1, 8 bits wide
  assign not_1_out = ~A;  // NOT_Gate not_1, 8 bits wide
  assign xor_1_out = A ^ B;  // XOR_Gate xor_1, 8 bits wide
  or or_2 (Carry, adder_1_cout, subtractor_1_bout);
  assign Result = decoder_1_out0 ? adder_1_out : 8'bz;  // Controlled_Buffer controlled_buffer_1
  assign Result = decoder_1_out1 ? subtractor_1_out : 8'bz;  // Controlled_Buffer controlled_buffer_2
  assign Result = decoder_1_out2 ? and_1_out : 8'bz;  // Controlled_Buffer controlled_buffer_3
  assign Result = decoder_1_out3 ? or_1_out : 8'bz;  // Controlled_Buffer controlled_buffer_4
  assign Result = decoder_1_out4 ? not_1_out : 8'bz;  // Controlled_Buffer controlled_buffer_5
  assign Result = decoder_1_out5 ? xor_1_out : 8'bz;  // Controlled_Buffer controlled_buffer_6
endmodule

// Срав.
module ComparatorMod (
  input  [7:0] L_d35cfc3e,
  input  [7:0] A,
  input  [7:0] B,
  output Result
);

  wire and_1_out, and_2_out, and_3_out, and_4_out, and_5_out, and_6_out, comparator_1_eq, comparator_1_gt,
       comparator_1_lt, comparator_2_eq, comparator_2_gt, comparator_2_lt, comparator_3_eq, comparator_3_gt,
       comparator_3_lt, comparator_4_eq, comparator_4_gt, comparator_4_lt, comparator_5_eq, comparator_5_gt,
       comparator_5_lt, comparator_6_eq, comparator_6_gt, comparator_6_lt, decoder_1_out0, decoder_1_out1,
       decoder_1_out2, decoder_1_out3, decoder_1_out4, decoder_1_out5, not_1_out, not_2_out, not_3_out,
       not_4_out, not_5_out, not_6_out, not_7_out, not_8_out, not_9_out, or_1_out, or_2_out, or_3_out;

  Decoder #(.enable("false"), .select(3)) decoder_1 (
    .out0(decoder_1_out0), .out1(decoder_1_out1), .out2(decoder_1_out2), .out3(decoder_1_out3),
    .out4(decoder_1_out4), .out5(decoder_1_out5), .sel(L_d35cfc3e[2:0]));  // open: out6, out7
  not not_1 (not_1_out, comparator_1_gt);
  Comparator comparator_1 (.a(A), .b(B), .gt(comparator_1_gt), .eq(comparator_1_eq), .lt(comparator_1_lt));
  not not_2 (not_2_out, comparator_1_lt);
  not not_3 (not_3_out, comparator_2_eq);
  Comparator comparator_2 (.a(A), .b(B), .gt(comparator_2_gt), .eq(comparator_2_eq), .lt(comparator_2_lt));
  not not_4 (not_4_out, comparator_3_gt);
  not not_5 (not_5_out, comparator_3_eq);
  Comparator comparator_3 (.a(A), .b(B), .gt(comparator_3_gt), .eq(comparator_3_eq), .lt(comparator_3_lt));
  not not_6 (not_6_out, comparator_4_gt);
  Comparator comparator_4 (.a(A), .b(B), .gt(comparator_4_gt), .eq(comparator_4_eq), .lt(comparator_4_lt));
  not not_7 (not_7_out, comparator_5_eq);
  Comparator comparator_5 (.a(A), .b(B), .gt(comparator_5_gt), .eq(comparator_5_eq), .lt(comparator_5_lt));
  not not_8 (not_8_out, comparator_5_lt);
  Comparator comparator_6 (.a(A), .b(B), .gt(comparator_6_gt), .eq(comparator_6_eq), .lt(comparator_6_lt));
  not not_9 (not_9_out, comparator_6_lt);
  and and_1 (and_1_out, not_1_out, comparator_1_eq, not_2_out);
  and and_2 (and_2_out, not_3_out, or_1_out);
  or or_1 (or_1_out, comparator_2_gt, comparator_2_lt);
  and and_3 (and_3_out, not_4_out, not_5_out, comparator_3_lt);
  and and_4 (and_4_out, not_6_out, or_2_out);
  or or_2 (or_2_out, comparator_4_eq, comparator_4_lt);
  and and_5 (and_5_out, comparator_5_gt, not_7_out, not_8_out);
  or or_3 (or_3_out, comparator_6_gt, comparator_6_eq);
  and and_6 (and_6_out, or_3_out, not_9_out);
  assign Result = decoder_1_out0 ? and_1_out : 1'bz;  // Controlled_Buffer controlled_buffer_1
  assign Result = decoder_1_out1 ? and_2_out : 1'bz;  // Controlled_Buffer controlled_buffer_2
  assign Result = decoder_1_out2 ? and_3_out : 1'bz;  // Controlled_Buffer controlled_buffer_3
  assign Result = decoder_1_out3 ? and_4_out : 1'bz;  // Controlled_Buffer controlled_buffer_4
  assign Result = decoder_1_out4 ? and_5_out : 1'bz;  // Controlled_Buffer controlled_buffer_5
  assign Result = decoder_1_out5 ? and_6_out : 1'bz;  // Controlled_Buffer controlled_buffer_6
endmodule

module RegisterMod (
  input  [7:0] Data,
  input  Save,
  input  Load,
  input  Clock,
  output [7:0] DataIfLoad,
  output [7:0] DataAlways
);

  wire and_1_out;

  Register Register8 (.D(Data), .en(1'b1), .clk(and_1_out), .Q(DataAlways));  // open: clr
  and and_1 (and_1_out, Save, Clock);
  assign DataIfLoad = Load ? DataAlways : 8'bz;  // Controlled_Buffer controlled_buffer_1
endmodule

module Equals (
  input  [7:0] A,
  input  [7:0] B,
  output res
);

  Comparator #(.mode("unsigned")) comparator_1 (.a(A), .b(B), .eq(res));  // open: gt, lt
endmodule

module eightbittoBCD (
  input  [7:0] in_1,
  output [3:0] firstdigit,
  output [3:0] seconddigit,
  output [3:0] thirddigit
);

  wire comparator_1_lt, comparator_2_gt;
  wire [7:0] divider_1_out, divider_1_rem, divider_2_out, divider_2_rem;

  Comparator #(.mode("unsigned")) comparator_1 (.a(8'h9), .b(in_1), .lt(comparator_1_lt));  // open: gt, eq
  Divider divider_1 (.a(in_1), .out(divider_1_out), .rem(divider_1_rem));  // open: b, upper
  Divider divider_2 (.a(divider_1_out), .b(8'ha), .out(divider_2_out), .rem(divider_2_rem));  // open: upper
  Comparator #(.mode("unsigned")) comparator_2 (.a(divider_1_out), .b(8'h9), .gt(comparator_2_gt));  // open: eq, lt
  Multiplexer #(.width(4)) multiplexer_1 (
    .in0(in_1[3:0]), .in1(divider_1_rem[3:0]), .out(firstdigit), .sel(comparator_1_lt));
  assign seconddigit = comparator_1_lt ? divider_2_out[3:0] : 4'bz;  // Controlled_Buffer controlled_buffer_1
  assign thirddigit = comparator_2_gt ? divider_2_rem[3:0] : 4'bz;  // Controlled_Buffer controlled_buffer_2
endmodule

module smallOR (
  input  in_1,
  input  in_2,
  output out_3
);

  or or_1 (out_3, in_1, in_2);
endmodule

module busControl (
  input  [7:0] in_1,
  input  [7:0] in_2,
  input  [7:0] in_3,
  input  [7:0] in_4,
  input  in_5,
  output [7:0] out_6,
  output [7:0] out_7,
  output [7:0] out_8,
  output [7:0] out_9
);

  assign out_9 = in_5 ? in_4 : 8'bz;  // Controlled_Buffer controlled_buffer_1
  assign out_6 = in_5 ? in_1 : 8'bz;  // Controlled_Buffer controlled_buffer_2
  assign out_7 = in_5 ? in_2 : 8'bz;  // Controlled_Buffer controlled_buffer_3
  assign out_8 = in_5 ? in_3 : 8'bz;  // Controlled_Buffer controlled_buffer_4
endmodule

module NCtoTF (
  input  A,
  output res
);


  assign res = A;
endmodule

module SumMod (
  input  CarryIN,
  input  [7:0] A,
  input  [7:0] B,
  output [7:0] Result,
  output CarryOUT,
  output HalfCarryOUT
);

  Adder #(.width(4)) adder_1 (.a(A[3:0]), .b(B[3:0]), .out(Result[3:0]), .cin(CarryIN), .cout(HalfCarryOUT));
  Adder #(.width(4)) adder_2 (.a(A[7:4]), .b(B[7:4]), .out(Result[7:4]), .cin(HalfCarryOUT), .cout(CarryOUT));
endmodule

module bigControledBuffer (
  input  enable,
  input  A,
  output B_0,
  output B_1,
  output B_2,
  output B_3,
  output B_4,
  output B_5,
  output B_6,
  output B_7
);

  assign B_0 = enable ? A : 1'bz;  // Controlled_Buffer controlled_buffer_1
  assign B_1 = enable ? A : 1'bz;  // Controlled_Buffer controlled_buffer_2
  assign B_2 = enable ? A : 1'bz;  // Controlled_Buffer controlled_buffer_3
  assign B_3 = enable ? A : 1'bz;  // Controlled_Buffer controlled_buffer_4
  assign B_4 = enable ? A : 1'bz;  // Controlled_Buffer controlled_buffer_5
  assign B_5 = enable ? A : 1'bz;  // Controlled_Buffer controlled_buffer_6
  assign B_6 = enable ? A : 1'bz;  // Controlled_Buffer controlled_buffer_7
  assign B_7 = enable ? A : 1'bz;  // Controlled_Buffer controlled_buffer_8
endmodule
